# Fritzing sketch fritzing-sketch (saved by Fritzing 1.0.0rc)

parts:
  Pico_H1 = Raspberry Pi Pico H
  Part1 = Adafruit MAX98357A I2S 3W Class D Amplifier [part_number="Adafruit #3006"]
  SP1 = SPEAKER [package=pcb_mount_speaker]  # not connected
  BUTTON1 = Arcade Button (blue)

nets:
  N1: Pico_H1.VBUS, Part1.VIN
  GND: Pico_H1.GND, Part1.GND, BUTTON1.no_name_yet#1
  N2: Pico_H1.GP22, BUTTON1.no_name_yet#2
  N3: Pico_H1.GP2, Part1.DIN
  N4: Pico_H1.GP1, Part1.LRCLK
  N5: Pico_H1.GP0, Part1.BCLK

notes:
  The arcade button with LED also requires a connection to power (VBUS - 5v) and ground to light up the LED.
  Put a 220ohm resistor between power and the anode of the LED on the button.
  Example:
  VBUS (Pin 40) → Resistor → LED Anode (+)

custom parts:
  Raspberry Pi Pico H: Raspberry Pi Pico H. Based around the RP2040 microcontroller the Pico H is a low cost microcontroller device bringing Raspberry Pi quality, cost, and easy of use to the microcontroller space.
  Adafruit MAX98357A I2S 3W Class D Amplifier: Listen to this good news - we now have an all in one digital audio amp breakout board that works incredibly well with the Raspberry Pi! If you're looking for an easy and low cost way to get you digital sound files bumpin' then the MAX08357 I2S Amp Breakout is for you. It takes standard I2S digital audio input and, not only decodes it into analog, but also amplifies it directly into a speaker.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
  Arcade Button (blue): Adafruit Arcade Button (blue)
